// Logisim project Pong.circ as structural Verilog: 4 circuits, main circuit main
module main (
  input  in_1,
  output [6:0] out_2
);

  wire clock_1_out;
  wire [9:0] players_1_outp1, players_1_outp2;

  Keyboard keyboard_1 (.re(in_1), .clr(clock_1_out), .data(out_2));  // open: clk, avail
  Clock clock_1 (.out(clock_1_out));
  DotMatrix #(.matrixcols(20), .matrixrows(10)) dotmatrix_1 (
    .col0(players_1_outp1), .col19(players_1_outp2));  // open: col1, col2, col3, col4, col5, col6, col7, col8, col9, col10, col11, col12, col13, col14, col15, col16, col17, col18
  Players players_1 (.In(out_2), .OutP1(players_1_outp1), .OutP2(players_1_outp2));
endmodule

module Players (
  input  [6:0] In,
  output [9:0] OutP1,
  output [9:0] OutP2
);

  wire \direção_1_enable , \direção_1_out , \direção_2_enable , \direção_2_out , DownP1, DownP2, UpP1, UpP2;

  Comparator #(.width(7)) comparator_1 (.a(7'b1110111), .b(In), .eq(UpP1));  // open: gt, lt
  Comparator #(.width(7)) comparator_2 (.a(7'b1110011), .b(In), .eq(DownP1));  // open: gt, lt
  Comparator #(.width(7)) comparator_3 (.a(7'b1101111), .b(In), .eq(UpP2));  // open: gt, lt
  Comparator #(.width(7)) comparator_4 (.a(7'b1101100), .b(In), .eq(DownP2));  // open: gt, lt
  \Direção  \direção_1  (.Up_In(UpP1), .Down_In(DownP1), .Out(\direção_1_out ), .Enable(\direção_1_enable ));
  \Direção  \direção_2  (.Up_In(UpP2), .Down_In(DownP2), .Out(\direção_2_out ), .Enable(\direção_2_enable ));
  Movimento movimento_1 (.In(\direção_1_out ), .Enable(\direção_1_enable ), .Out(OutP1));
  Movimento movimento_2 (.In(\direção_2_out ), .Enable(\direção_2_enable ), .Out(OutP2));

  // Notes on the sheet:
  //   W
  //   S
  //   O
  //   L
endmodule

module \Direção  (
  input  Up_In,
  input  Down_In,
  output Out,
  output Enable
);

  wire and_1_out, xor_1_out;

  or or_1 (Enable, Up_In, Down_In);
  xor xor_1 (xor_1_out, Up_In, Down_In);
  and and_1 (and_1_out, Up_In, ~Down_In);  // AND_Gate
  and and_2 (Out, xor_1_out, and_1_out);
endmodule

module Movimento (
  input  In,
  input  Enable,
  output [9:0] Out
);

  wire and_3_out, clock_1_out, comparator_1_lt, comparator_2_lt, d_ff_1_q, not_1_out;
  wire [0:0] and_1_out, and_2_out;
  wire [9:0] multiplexer_1_out, multiplexer_2_out, multiplexer_3_out, shifter_1_out, shifter_2_out;

  Clock clock_1 (.out(clock_1_out));
  not not_1 (not_1_out, In);
  and and_1 (and_1_out[0], In, Enable);
  and and_2 (and_2_out[0], not_1_out, Enable);
  D_Flip_Flop d_ff_1 (.clk(clock_1_out), .D(clock_1_out), .Q(d_ff_1_q));  // open: Qn, preset, en, reset
  Multiplexer #(.width(10), .enable("false")) multiplexer_1 (
    .in0(multiplexer_2_out), .in1(Out), .out(multiplexer_1_out), .sel(and_2_out[0]));
  Multiplexer #(.width(10), .enable("false")) multiplexer_2 (
    .in0(10'hf), .in1(Out), .out(multiplexer_2_out), .sel(d_ff_1_q));
  Shifter #(.width(10), .shift("lr")) shifter_1 (
    .in(multiplexer_1_out), .\dist ({3'b000, and_2_out[0]}), .out(shifter_1_out));
  Multiplexer #(.width(10), .enable("false")) multiplexer_3 (
    .in0(shifter_1_out), .in1(shifter_2_out), .out(multiplexer_3_out), .sel(and_1_out[0]));
  Shifter #(.width(10)) shifter_2 (.in(multiplexer_2_out), .\dist ({3'b000, and_1_out[0]}), .out(shifter_2_out));
  Comparator #(.width(10)) comparator_1 (.a(10'h7), .b(shifter_1_out), .lt(comparator_1_lt));  // open: gt, eq
  Comparator #(.width(10)) comparator_2 (.a(10'h380), .b(shifter_2_out), .lt(comparator_2_lt));  // open: gt, eq
  and and_3 (and_3_out, comparator_1_lt, comparator_2_lt);
  Register #(.width(10)) register_1 (.D(multiplexer_3_out), .en(and_3_out), .Q(Out), .clk(clock_1_out));  // open: clr
endmodule
